// Logisim project P1Q1-Subtractor.circ as structural Verilog: 1 circuit, main circuit main
module main (
  input  A,
  input  B,
  input  Bin,
  output D,
  output Bout
);

  wire and_1_out, and_2_out, and_3_out, not_1_out, xor_1_out;

  not not_1 (not_1_out, A);
  xor xor_1 (xor_1_out, A, B);
  xor xor_2 (D, xor_1_out, Bin);
  and and_1 (and_1_out, not_1_out, B);
  and and_2 (and_2_out, not_1_out, Bin);
  and and_3 (and_3_out, Bin, B);
  or or_1 (Bout, and_1_out, and_2_out, and_3_out);
endmodule
