// Logisim project DOWN_Counter.circ as structural Verilog: 1 circuit, main circuit main
module main (
  input  PRESET,
  input  EN,
  input  RESET,
  output Q0,
  output Q1,
  output Q2,
  output Q3
);

  wire and_1_out, and_2_out, CLK_out, JK0_qn, JK1_qn, JK2_qn, pull_resistor_1_node;

  Pull_Resistor #(.pull(1)) pull_resistor_1 (.node(pull_resistor_1_node));
  Clock CLK (.out(CLK_out));
  J_K_Flip_Flop JK0 (
    .J(pull_resistor_1_node), .clk(CLK_out), .K(pull_resistor_1_node), .Q(Q0), .Qn(JK0_qn), .preset(PRESET),
    .en(EN), .reset(RESET));
  J_K_Flip_Flop JK1 (
    .J(JK0_qn), .clk(CLK_out), .K(JK0_qn), .Q(Q1), .Qn(JK1_qn), .preset(PRESET), .en(EN), .reset(RESET));
  and and_1 (and_1_out, JK1_qn, JK0_qn);
  J_K_Flip_Flop JK2 (
    .J(and_1_out), .clk(CLK_out), .K(and_1_out), .Q(Q2), .Qn(JK2_qn), .preset(PRESET), .en(EN), .reset(RESET));
  and and_2 (and_2_out, JK2_qn, and_1_out);
  J_K_Flip_Flop JK3 (
    .J(and_2_out), .clk(CLK_out), .K(and_2_out), .Q(Q3), .preset(PRESET), .en(EN), .reset(RESET));  // open: Qn

  // Notes on the sheet:
  //   Down Counter
  //   Prajapati Yash P. (BDA)
  //   20162121023
endmodule
