// Logisim project UP_Counter.circ as structural Verilog: 1 circuit, main circuit main
module main (
  input  PRESET,
  input  EN,
  input  RESET,
  output Q0,
  output Q1,
  output Q2,
  output Q3
);

  wire and_1_out, and_2_out, CLK_out, pull_resistor_1_node;

  Clock CLK (.out(CLK_out));
  Pull_Resistor #(.pull(1)) pull_resistor_1 (.node(pull_resistor_1_node));
  J_K_Flip_Flop JK0 (
    .J(pull_resistor_1_node), .clk(CLK_out), .K(pull_resistor_1_node), .Q(Q0), .preset(PRESET), .en(EN),
    .reset(RESET));  // open: Qn
  J_K_Flip_Flop JK1 (.J(Q0), .clk(CLK_out), .K(Q0), .Q(Q1), .preset(PRESET), .en(EN), .reset(RESET));  // open: Qn
  and and_1 (and_1_out, Q0, Q1);
  and and_2 (and_2_out, and_1_out, Q2);
  J_K_Flip_Flop JK2 (
    .J(and_1_out), .clk(CLK_out), .K(and_1_out), .Q(Q2), .preset(PRESET), .en(EN), .reset(RESET));  // open: Qn
  J_K_Flip_Flop JK3 (
    .J(and_2_out), .clk(CLK_out), .K(and_2_out), .Q(Q3), .preset(PRESET), .en(EN), .reset(RESET));  // open: Qn

  // Notes on the sheet:
  //   Up Counter
  //   Prajapati Yash P.(BDA)
  //   20162121023
endmodule
