// Logisim project UP_DOWN_Counter.circ as structural Verilog: 1 circuit, main circuit main
module main (
  input  Up_Down,
  input  PRESET,
  input  EN,
  input  RESET,
  output Q0,
  output Q1,
  output Q2,
  output Q3
);

  wire and_1_out, and_2_out, and_3_out, and_4_out, and_5_out, and_6_out, CLK_out, JK0_qn, JK1_qn, JK2_qn,
       not_1_out, or_1_out, or_2_out, or_3_out, pull_resistor_1_node;

  Clock CLK (.out(CLK_out));
  not not_1 (not_1_out, Up_Down);
  Pull_Resistor #(.pull(1)) pull_resistor_1 (.node(pull_resistor_1_node));
  J_K_Flip_Flop JK0 (
    .J(pull_resistor_1_node), .clk(CLK_out), .K(pull_resistor_1_node), .Q(Q0), .Qn(JK0_qn), .preset(PRESET),
    .en(EN), .reset(RESET));
  and and_1 (and_1_out, not_1_out, Q0);
  and and_2 (and_2_out, JK0_qn, Up_Down);
  J_K_Flip_Flop JK1 (
    .J(or_1_out), .clk(CLK_out), .K(or_1_out), .Q(Q1), .Qn(JK1_qn), .preset(PRESET), .en(EN), .reset(RESET));
  or or_1 (or_1_out, and_1_out, and_2_out);
  and and_3 (and_3_out, not_1_out, and_1_out, Q1);
  and and_4 (and_4_out, JK1_qn, and_2_out, Up_Down);
  or or_2 (or_2_out, and_3_out, and_4_out);
  J_K_Flip_Flop JK2 (
    .J(or_2_out), .clk(CLK_out), .K(or_2_out), .Q(Q2), .Qn(JK2_qn), .preset(PRESET), .en(EN), .reset(RESET));
  and and_5 (and_5_out, not_1_out, and_3_out, Q2);
  or or_3 (or_3_out, and_5_out, and_6_out);
  and and_6 (and_6_out, JK2_qn, and_4_out, Up_Down);
  J_K_Flip_Flop JK3 (
    .J(or_3_out), .clk(CLK_out), .K(or_3_out), .Q(Q3), .preset(PRESET), .en(EN), .reset(RESET));  // open: Qn

  // Notes on the sheet:
  //   Prajapati Yash P. (BDA)
  //   UP/DOWN Counter
  //   20162121023
endmodule
