// Logisim project Decrement.circ as structural Verilog: 2 circuits, main circuit main
module main (
  input  in_1,
  input  in_2,
  input  in_3,
  input  in_4,
  output out_5,
  output out_6,
  output out_7,
  output out_8
);

  wire fa_1_cout, fa_2_cout, fa_3_cout;

  FA fa_1 (.A(in_1), .B(1'b1), .Cin(1'b0), .S(out_5), .Cout(fa_1_cout));
  FA fa_2 (.A(in_2), .B(1'b1), .Cin(fa_1_cout), .S(out_6), .Cout(fa_2_cout));
  FA fa_3 (.A(in_3), .B(1'b1), .Cin(fa_2_cout), .S(out_7), .Cout(fa_3_cout));
  FA fa_4 (.A(in_4), .B(1'b1), .Cin(fa_3_cout), .S(out_8));  // open: Cout

  // Notes on the sheet:
  //   Decrement
  //   Prajapati Yash P (20162121023)
endmodule

module FA (
  input  A,
  input  B,
  input  Cin,
  output S,
  output Cout
);

  wire and_1_out, and_2_out, and_3_out, xor_1_out;

  xor xor_1 (xor_1_out, A, B);
  and and_1 (and_1_out, A, B);
  and and_2 (and_2_out, A, Cin);
  and and_3 (and_3_out, Cin, B);
  xor xor_2 (S, xor_1_out, Cin);
  or or_1 (Cout, and_1_out, and_2_out, and_3_out);

  // Notes on the sheet:
  //   Full Adder
endmodule
