// Logisim project Increment.circ as structural Verilog: 2 circuits, main circuit main
module main (
  input  A0,
  input  A1,
  input  A2,
  input  A3,
  output S0,
  output S1,
  output S2,
  output S3,
  output Cout
);

  wire fa_1_carry, fa_2_carry, fa_3_carry;

  FA fa_1 (.A(A0), .B(1'b0), .Cin(1'b1), .SUM(S0), .CARRY(fa_1_carry));
  FA fa_2 (.A(A1), .B(1'b0), .Cin(fa_1_carry), .SUM(S1), .CARRY(fa_2_carry));
  FA fa_3 (.A(A2), .B(1'b0), .Cin(fa_2_carry), .SUM(S2), .CARRY(fa_3_carry));
  FA fa_4 (.A(A3), .B(1'b0), .Cin(fa_3_carry), .SUM(S3), .CARRY(Cout));

  // Notes on the sheet:
  //   Incrementer
  //   PRAJAPATI YASH P (20162121023)
endmodule

module FA (
  input  A,
  input  B,
  input  Cin,
  output SUM,
  output CARRY
);

  wire AND1_out, AND2_out, AND3_out;

  ExactlyOne XOR (.out(SUM), .in0(A), .in1(B), .in2(Cin));
  and AND1 (AND1_out, A, B);
  and AND2 (AND2_out, A, Cin);
  and AND3 (AND3_out, B, Cin);
  or or_1 (CARRY, AND1_out, AND2_out, AND3_out);

  // Notes on the sheet:
  //   Full Adder
endmodule
