// Logisim project FS.circ as structural Verilog: 1 circuit, main circuit FS
module FS (
  input  A,
  input  B,
  input  Bin,
  output D,
  output Bout
);

  wire and_1_out, and_2_out, not_1_out, not_2_out, xor_1_out;

  not not_1 (not_1_out, A);
  xor xor_1 (xor_1_out, A, B);
  and and_1 (and_1_out, B, not_1_out);
  not not_2 (not_2_out, xor_1_out);
  xor xor_2 (D, xor_1_out, Bin);
  and and_2 (and_2_out, Bin, not_2_out);
  or or_1 (Bout, and_2_out, and_1_out);

  // Notes on the sheet:
  //   Full Subtractor
  //   Prajapati Yash P (20162121023)
endmodule
