// Logisim project HS.circ as structural Verilog: 1 circuit, main circuit HS
module HS (
  input  A,
  input  B,
  output D,
  output Bout
);

  wire not_1_out;

  not not_1 (not_1_out, A);
  xor xor_1 (D, A, B);
  and and_1 (Bout, B, not_1_out);

  // Notes on the sheet:
  //   Half Subtractor
  //   Prajapati Yash P (20162121023)
endmodule
