// Logisim project Ripple Subtractor_FA.circ as structural Verilog: 1 circuit, main circuit main
module main (
  input  B3,
  input  A3,
  input  B2,
  input  A2,
  input  B1,
  input  A1,
  input  B0,
  input  A0,
  input  Cin,
  input  B3_2,
  input  A3_2,
  input  B2_2,
  input  A2_2,
  input  B1_2,
  input  A1_2,
  input  B0_2,
  input  A0_2,
  input  Cin_2,
  output Cout,
  output S3,
  output S2,
  output S1,
  output S0,
  output Cout_2,
  output S3_2,
  output S2_2,
  output S1_2,
  output S0_2
);

  wire main_3_bout, main_4_bout, main_5_bout, main_6_bout, main_7_bout, main_8_bout, not_1_out, not_2_out,
       not_3_out, not_4_out, xor_1_out, xor_2_out, xor_3_out, xor_4_out;

  not not_1 (not_1_out, B3);
  P1Q1_Adder_main main_1 (.A(A3), .B(not_1_out), .Cin(main_3_bout), .S(S3), .Bout(Cout));
  xor xor_1 (xor_1_out, B3_2, Cin_2);
  P1Q1_Adder_main main_2 (.A(A3_2), .B(xor_1_out), .Cin(main_4_bout), .S(S3_2), .Bout(Cout_2));
  not not_2 (not_2_out, B2);
  P1Q1_Adder_main main_3 (.A(A2), .B(not_2_out), .Cin(main_5_bout), .S(S2), .Bout(main_3_bout));
  xor xor_2 (xor_2_out, B2_2, Cin_2);
  P1Q1_Adder_main main_4 (.A(A2_2), .B(xor_2_out), .Cin(main_6_bout), .S(S2_2), .Bout(main_4_bout));
  not not_3 (not_3_out, B1);
  xor xor_3 (xor_3_out, B1_2, Cin_2);
  P1Q1_Adder_main main_5 (.A(A1), .B(not_3_out), .Cin(main_7_bout), .S(S1), .Bout(main_5_bout));
  P1Q1_Adder_main main_6 (.A(A1_2), .B(xor_3_out), .Cin(main_8_bout), .S(S1_2), .Bout(main_6_bout));
  not not_4 (not_4_out, B0);
  P1Q1_Adder_main main_7 (.A(A0), .B(not_4_out), .Cin(Cin), .S(S0), .Bout(main_7_bout));
  xor xor_4 (xor_4_out, B0_2, Cin_2);
  P1Q1_Adder_main main_8 (.A(A0_2), .B(xor_4_out), .Cin(Cin_2), .S(S0_2), .Bout(main_8_bout));

  // Notes on the sheet:
  //   Ripple Carry Subtractor
  //   Prajapati Yash P (20162121023)
  //   Prajapati Yash P (20162121023)
  //   Parallel Adder/Subtractor
endmodule
