// Logisim project Ripple Subtractor_FS-HS.circ as structural Verilog: 1 circuit, main circuit RCS-FS-HS
module RCS_FS_HS (
  input  B3,
  input  A3,
  input  B2,
  input  A2,
  input  B1,
  input  A1,
  input  B0,
  input  A0,
  output Bout,
  output D3,
  output D2,
  output D1,
  output D0
);

  wire FS_1_bout, FS_2_bout, HS_0_bout;

  FS FS_3 (.A(A3), .B(B3), .D(D3), .Bin(FS_2_bout), .Bout(Bout));
  FS FS_2 (.A(A2), .B(B2), .D(D2), .Bin(FS_1_bout), .Bout(FS_2_bout));
  FS FS_1 (.A(A1), .B(B1), .D(D1), .Bin(HS_0_bout), .Bout(FS_1_bout));
  HS HS_0 (.A(A0), .B(B0), .D(D0), .Bout(HS_0_bout));

  // Notes on the sheet:
  //   Ripple Carry Subtractor
  //   Prajapati Yash P (20162121023)
endmodule
