// Logisim project LACG.circ as structural Verilog: 1 circuit, main circuit main
module main (
  input  G3,
  input  P3,
  input  G2,
  input  P2,
  input  G1,
  input  P1,
  input  G0,
  input  P0,
  input  Cin,
  output Cout,
  output C3,
  output C2,
  output C1
);

  wire AND0_out, AND1_out, AND2_out, AND3_out, AND4_out, AND5_out, AND6_out, AND7_out, AND8_out, AND9_out;

  and AND9 (AND9_out, P3, G2);
  and AND8 (AND8_out, P3, P2, G1);
  and AND7 (AND7_out, P3, P2, P1, G0);
  and AND6 (AND6_out, P3, P2, P1, P0, Cin);
  and AND5 (AND5_out, P2, G1);
  and AND4 (AND4_out, P2, P1, G0);
  and AND3 (AND3_out, P2, P1, P0, Cin);
  and AND2 (AND2_out, P1, G0);
  and AND1 (AND1_out, P1, P0, Cin);
  and AND0 (AND0_out, P0, Cin);
  or OR3 (Cout, G3, AND9_out, AND8_out, AND7_out, AND6_out);
  or OR2 (C3, G2, AND5_out, AND4_out, AND3_out);
  or OR1 (C2, G1, AND2_out, AND1_out);
  or OR0 (C1, G0, AND0_out);

  // Notes on the sheet:
  //   Look Ahead Carry Generator
  //   Prajapati Yash P. (20162121023)
endmodule
