// Logisim project 2-Bit Multiplier.circ as structural Verilog: 1 circuit, main circuit main
module main (
  input  A1,
  input  A0,
  input  B1,
  input  B0,
  output M3,
  output M2,
  output M1,
  output M0
);

  wire AND1_out, AND2_out, AND3_out, HA0_cout;

  and AND3 (AND3_out, B1, A1);
  Half_Adder_main HA1 (.A(HA0_cout), .B(AND3_out), .S(M2), .Cout(M3));
  and AND1 (AND1_out, B0, A1);
  and AND2 (AND2_out, B1, A0);
  Half_Adder_main HA0 (.A(AND1_out), .B(AND2_out), .S(M1), .Cout(HA0_cout));
  and AND0 (M0, B0, A0);

  // Notes on the sheet:
  //   20162121023
  //   2-Bit Multiplier
  //   Prajapati Yash P. 
endmodule
