// Logisim project 4-Bit Multiplier.circ as structural Verilog: 1 circuit, main circuit main
module main (
  input  a3,
  input  a2,
  input  a1,
  input  a0,
  input  b3,
  input  b2,
  input  b1,
  input  b0,
  output out_9,
  output out_10,
  output out_11,
  output out_12,
  output out_13,
  output out_14,
  output out_15,
  output out_16
);

  wire AND1_out, AND2_out, AND3_out, AND4_out, AND5_out, AND6_out, AND7_out, AND8_out, AND9_out, AND10_out,
       AND11_out, AND12_out, AND13_out, AND14_out, AND15_out, FA0_bout, FA1_bout, FA1_s, FA2_bout, FA3_bout,
       FA3_s, FA4_bout, FA4_s, FA5_bout, FA5_s, FA6_bout, HA0_cout, HA1_cout, HA1_s, HA2_cout, HA2_s,
       HA3_cout;

  and AND15 (AND15_out, b3, a3);
  Full_Adder_main FA7 (.A(FA5_bout), .B(AND15_out), .Cin(FA6_bout), .S(out_10), .Bout(out_9));
  and AND13 (AND13_out, b2, a3);
  and AND14 (AND14_out, b3, a2);
  Full_Adder_main FA5 (.A(AND13_out), .B(AND14_out), .Cin(FA3_bout), .S(FA5_s), .Bout(FA5_bout));
  Full_Adder_main FA6 (.A(FA4_bout), .B(FA5_s), .Cin(HA3_cout), .S(out_11), .Bout(FA6_bout));
  and AND12 (AND12_out, b3, a1);
  and AND11 (AND11_out, b2, a2);
  and AND10 (AND10_out, b1, a3);
  Full_Adder_main FA3 (.A(AND10_out), .B(AND11_out), .Cin(HA2_cout), .S(FA3_s), .Bout(FA3_bout));
  Full_Adder_main FA4 (.A(FA3_s), .B(AND12_out), .Cin(FA1_bout), .S(FA4_s), .Bout(FA4_bout));
  Half_Adder_main HA3 (.A(FA2_bout), .B(FA4_s), .S(out_12), .Cout(HA3_cout));
  and AND8 (AND8_out, b2, a1);
  and AND9 (AND9_out, b3, a0);
  and AND7 (AND7_out, b1, a2);
  Half_Adder_main HA2 (.A(AND6_out), .B(AND7_out), .S(HA2_s), .Cout(HA2_cout));
  Full_Adder_main FA1 (.A(HA2_s), .B(AND8_out), .Cin(HA1_cout), .S(FA1_s), .Bout(FA1_bout));
  and AND6 (AND6_out, b0, a3);
  and AND5 (AND5_out, b2, a0);
  Full_Adder_main FA2 (.A(FA1_s), .B(AND9_out), .Cin(FA0_bout), .S(out_13), .Bout(FA2_bout));
  and AND4 (AND4_out, b1, a1);
  Half_Adder_main HA1 (.A(AND3_out), .B(AND4_out), .S(HA1_s), .Cout(HA1_cout));
  Full_Adder_main FA0 (.A(HA1_s), .B(AND5_out), .Cin(HA0_cout), .S(out_14), .Bout(FA0_bout));
  and AND2 (AND2_out, b1, a0);
  and AND3 (AND3_out, b0, a2);
  and AND0 (out_16, b0, a0);
  and AND1 (AND1_out, b0, a1);
  Half_Adder_main HA0 (.A(AND1_out), .B(AND2_out), .S(out_15), .Cout(HA0_cout));

  // Notes on the sheet:
  //   20162121023
  //   4-Bit Multiplier
  //   Prajapati Yash P.
  //   BDA_Batch-23
endmodule
