// Logisim project 5-Bit Adder.circ as structural Verilog: 1 circuit, main circuit main
module main (
  input  B4,
  input  A4,
  input  B3,
  input  A3,
  input  B2,
  input  A2,
  input  B1,
  input  A1,
  input  B0,
  input  A0,
  input  Cin,
  output Cout,
  output S4,
  output S3,
  output S2,
  output S1,
  output S0
);

  wire adder_2_cout, adder_3_cout, adder_4_cout, adder_5_cout;

  LED led_1 (.in(Cout));
  Adder #(.width(1)) adder_1 (.a(A4), .b(B4), .out(S4), .cin(adder_2_cout), .cout(Cout));
  LED led_2 (.in(S4));
  Adder #(.width(1)) adder_2 (.a(A3), .b(B3), .out(S3), .cin(adder_3_cout), .cout(adder_2_cout));
  LED led_3 (.in(S3));
  Adder #(.width(1)) adder_3 (.a(A2), .b(B2), .out(S2), .cin(adder_4_cout), .cout(adder_3_cout));
  LED led_4 (.in(S2));
  Adder #(.width(1)) adder_4 (.a(A1), .b(B1), .out(S1), .cin(adder_5_cout), .cout(adder_4_cout));
  LED led_5 (.in(S1));
  Adder #(.width(1)) adder_5 (.a(A0), .b(B0), .out(S0), .cin(Cin), .cout(adder_5_cout));
  LED led_6 (.in(S0));

  // Notes on the sheet:
  //   Prajapati Yash P.
  //   20162121023(BDA_Batch-23)
endmodule
