// Logisim project Addition of 3 4-Bit No.circ as structural Verilog: 1 circuit, main circuit main
module main (
  input  A3,
  input  A2,
  input  A1,
  input  A0,
  input  B3,
  input  B2,
  input  B1,
  input  B0,
  input  Cin,
  input  C3,
  input  C2,
  input  C1,
  input  C0,
  output Cout,
  output S4,
  output S3,
  output S2,
  output S1,
  output S0
);

  wire FA0_bout, FA1_bout, FA1_s, FA2_bout, FA2_s, FA3_bout, FA3_s;

  Full_Adder_main FA3 (.A(A3), .B(B3), .Cin(C3), .S(FA3_s), .Bout(FA3_bout));
  _4_Bit_Adder_main main_1 (
    .Cout(Cout), .B3(1'b0), .A3(FA3_bout), .B2(FA3_s), .A2(FA2_bout), .B1(FA2_s), .A1(FA1_bout), .B0(FA1_s),
    .A0(FA0_bout), .Cin(Cin), .S3(S4), .S2(S3), .S1(S2), .S0(S1));
  Full_Adder_main FA2 (.A(A2), .B(B2), .Cin(C2), .S(FA2_s), .Bout(FA2_bout));
  Full_Adder_main FA1 (.A(A1), .B(B1), .Cin(C1), .S(FA1_s), .Bout(FA1_bout));
  Full_Adder_main FA0 (.A(A0), .B(B0), .Cin(C0), .S(S0), .Bout(FA0_bout));

  // Notes on the sheet:
  //   Prajapati Yash P.
  //   20162121023 (BDA_Batch-23)
  //   Addition of 3 4-Bit Numbers
endmodule
