// Logisim project Addition of 5 4-Bit No.circ as structural Verilog: 1 circuit, main circuit main
module main (
  input  A3,
  input  A2,
  input  A1,
  input  A0,
  input  E3,
  input  E2,
  input  E1,
  input  E0,
  input  B3,
  input  B2,
  input  B1,
  input  B0,
  input  C3,
  input  C2,
  input  C1,
  input  C0,
  input  D3,
  input  D2,
  input  D1,
  input  D0,
  output Cout,
  output S5,
  output S4,
  output S3,
  output S2,
  output S1,
  output S0
);

  wire main_1_bout, main_1_s, main_2_bout, main_2_s, main_3_bout, main_3_s, main_4_bout, main_4_s,
       main_5_bout, main_5_s, main_6_bout, main_6_s, main_8_bout, main_8_s, main_9_cout, main_9_s0,
       main_9_s1, main_9_s2, main_9_s3, main_10_bout, main_10_s, main_11_bout;

  Full_Adder_main main_1 (.A(A3), .B(B3), .Cin(C3), .S(main_1_s), .Bout(main_1_bout));
  Full_Adder_main main_2 (.A(A2), .B(B2), .Cin(C2), .S(main_2_s), .Bout(main_2_bout));
  Full_Adder_main main_3 (.A(A1), .B(B1), .Cin(C1), .S(main_3_s), .Bout(main_3_bout));
  Full_Adder_main main_4 (.A(A0), .B(B0), .Cin(C0), .S(main_4_s), .Bout(main_4_bout));
  Full_Adder_main main_5 (.A(main_9_cout), .B(1'b0), .Cin(main_1_bout), .S(main_5_s), .Bout(main_5_bout));
  Full_Adder_main main_6 (.A(main_9_s3), .B(main_1_s), .Cin(main_2_bout), .S(main_6_s), .Bout(main_6_bout));
  _5_Bit_Adder_main main_7 (
    .B3(main_5_s), .A3(main_6_bout), .B2(main_6_s), .A2(main_8_bout), .B1(main_8_s), .A1(main_10_bout),
    .B0(main_10_s), .A0(main_11_bout), .Cin(1'b0), .S3(S4), .S2(S3), .S1(S2), .S0(S1), .B4(1'b0),
    .A4(main_5_bout), .Cout(Cout), .S4(S5));
  Full_Adder_main main_8 (.A(main_9_s2), .B(main_2_s), .Cin(main_3_bout), .S(main_8_s), .Bout(main_8_bout));
  _4_Bit_Adder_main main_9 (
    .Cout(main_9_cout), .B3(E3), .A3(D3), .B2(E2), .A2(D2), .B1(E1), .A1(D1), .B0(E0), .A0(D0), .Cin(1'b0),
    .S3(main_9_s3), .S2(main_9_s2), .S1(main_9_s1), .S0(main_9_s0));
  Full_Adder_main main_10 (.A(main_9_s1), .B(main_3_s), .Cin(main_4_bout), .S(main_10_s), .Bout(main_10_bout));
  Full_Adder_main main_11 (.A(main_9_s0), .B(main_4_s), .Cin(1'b0), .S(S0), .Bout(main_11_bout));

  // Notes on the sheet:
  //   Prajapati Yash P.
  //   FA
  //   FA
  //   FA
  //   FA
  //   20162121023 (BDA_Batch-23)
  //   FA
  //   FA
  //   FA
  //   FA
  //   FA
  //   Addition of five 4-Bit Nos.
endmodule
