// Logisim project Addition7Bits.circ as structural Verilog: 1 circuit, main circuit main
module main (
  input  G,
  input  A,
  input  B,
  input  C,
  input  D,
  input  E,
  input  F,
  output S0,
  output S1,
  output Cout
);

  wire FA0_bout, FA0_s, FA1_bout, FA1_s, FA2_bout;

  Full_Adder_main FA0 (.A(A), .B(B), .Cin(C), .S(FA0_s), .Bout(FA0_bout));
  Full_Adder_main FA1 (.A(D), .B(E), .Cin(F), .S(FA1_s), .Bout(FA1_bout));
  Full_Adder_main FA2 (.A(G), .B(FA0_s), .Cin(FA1_s), .S(S0), .Bout(FA2_bout));
  Full_Adder_main FA3 (.A(FA2_bout), .B(FA0_bout), .Cin(FA1_bout), .S(S1), .Bout(Cout));

  // Notes on the sheet:
  //   20162121023
  //   BDA_Batch-23
  //   Prajapati Yash P.
  //   Addition of 7 Bits
endmodule
