// Logisim project 16Bit_Mem_Cell.circ as structural Verilog: 1 circuit, main circuit main
module main (
  input  D0,
  input  D1,
  input  D2,
  input  D3,
  input  B,
  input  A,
  input  CS,
  input  CLK,
  input  R_W_BAR,
  output Q0,
  output Q1,
  output Q2,
  output Q3
);

  wire main_1_q0, main_1_q1, main_1_q2, main_1_q3, W00_d_out, W01_d_out, W02_d_out, W03_d_out, W10_d_out,
       W11_d_out, W12_d_out, W13_d_out, W20_d_out, W21_d_out, W22_d_out, W23_d_out, W30_d_out, W31_d_out,
       W32_d_out, W33_d_out;

  DECODER_main main_1 (.Q3(main_1_q3), .Q2(main_1_q2), .Q1(main_1_q1), .Q0(main_1_q0), .EN(CS), .B(B), .A(A));
  _1Bit_Mem_Cell_main W30 (.SELECT(main_1_q3), .D_IN(D0), .CLK(CLK), .R_W_BAR(R_W_BAR), .D_OUT(W30_d_out));
  _1Bit_Mem_Cell_main W20 (.SELECT(main_1_q2), .D_IN(D0), .CLK(CLK), .R_W_BAR(R_W_BAR), .D_OUT(W20_d_out));
  _1Bit_Mem_Cell_main W10 (.SELECT(main_1_q1), .D_IN(D0), .CLK(CLK), .R_W_BAR(R_W_BAR), .D_OUT(W10_d_out));
  _1Bit_Mem_Cell_main W00 (.SELECT(main_1_q0), .D_IN(D0), .CLK(CLK), .R_W_BAR(R_W_BAR), .D_OUT(W00_d_out));
  or or_1 (Q0, W00_d_out, W10_d_out, W20_d_out, W30_d_out);
  _1Bit_Mem_Cell_main W31 (.SELECT(main_1_q3), .D_IN(D1), .CLK(CLK), .R_W_BAR(R_W_BAR), .D_OUT(W31_d_out));
  _1Bit_Mem_Cell_main W21 (.SELECT(main_1_q2), .D_IN(D1), .CLK(CLK), .R_W_BAR(R_W_BAR), .D_OUT(W21_d_out));
  _1Bit_Mem_Cell_main W11 (.SELECT(main_1_q1), .D_IN(D1), .CLK(CLK), .R_W_BAR(R_W_BAR), .D_OUT(W11_d_out));
  _1Bit_Mem_Cell_main W01 (.SELECT(main_1_q0), .D_IN(D1), .CLK(CLK), .R_W_BAR(R_W_BAR), .D_OUT(W01_d_out));
  or or_2 (Q1, W01_d_out, W11_d_out, W21_d_out, W31_d_out);
  _1Bit_Mem_Cell_main W32 (.SELECT(main_1_q3), .D_IN(D2), .CLK(CLK), .R_W_BAR(R_W_BAR), .D_OUT(W32_d_out));
  _1Bit_Mem_Cell_main W22 (.SELECT(main_1_q2), .D_IN(D2), .CLK(CLK), .R_W_BAR(R_W_BAR), .D_OUT(W22_d_out));
  _1Bit_Mem_Cell_main W12 (.SELECT(main_1_q1), .D_IN(D2), .CLK(CLK), .R_W_BAR(R_W_BAR), .D_OUT(W12_d_out));
  _1Bit_Mem_Cell_main W02 (.SELECT(main_1_q0), .D_IN(D2), .CLK(CLK), .R_W_BAR(R_W_BAR), .D_OUT(W02_d_out));
  or or_3 (Q2, W02_d_out, W12_d_out, W22_d_out, W32_d_out);
  _1Bit_Mem_Cell_main W33 (.SELECT(main_1_q3), .D_IN(D3), .CLK(CLK), .R_W_BAR(R_W_BAR), .D_OUT(W33_d_out));
  _1Bit_Mem_Cell_main W23 (.SELECT(main_1_q2), .D_IN(D3), .CLK(CLK), .R_W_BAR(R_W_BAR), .D_OUT(W23_d_out));
  _1Bit_Mem_Cell_main W13 (.SELECT(main_1_q1), .D_IN(D3), .CLK(CLK), .R_W_BAR(R_W_BAR), .D_OUT(W13_d_out));
  _1Bit_Mem_Cell_main W03 (.SELECT(main_1_q0), .D_IN(D3), .CLK(CLK), .R_W_BAR(R_W_BAR), .D_OUT(W03_d_out));
  or or_4 (Q3, W03_d_out, W13_d_out, W23_d_out, W33_d_out);

  // Notes on the sheet:
  //   20162121023
  //   Batch-23
  //   Addressing Lines
  //   Prajapati Yash P.
  //   Data Lines
  //   Data Output
  //   WORD 3
  //   WORD 2
  //   WORD 1
  //   WORD 0
  //   16-Bit Memory Cell
endmodule
