// Logisim project 1Bit_Mem_Cell.circ as structural Verilog: 1 circuit, main circuit main
module main (
  input  SELECT,
  input  D_IN,
  input  CLK,
  input  R_W_BAR,
  output D_OUT
);

  wire AND0_out, AND1_out, main_1_q, not_1_out, not_2_out;

  not not_1 (not_1_out, D_IN);
  not not_2 (not_2_out, R_W_BAR);
  and AND0 (AND0_out, not_2_out, SELECT, D_IN, CLK);
  and AND1 (AND1_out, CLK, not_1_out, SELECT, not_2_out);
  SR_FF_main main_1 (.S(AND0_out), .R(AND1_out), .Q(main_1_q));  // open: Q_BAR
  and AND2 (D_OUT, SELECT, main_1_q, R_W_BAR);

  // Notes on the sheet:
  //   20162121023
  //   Batch-23
  //   Prajapati Yash P.
  //   1-Bit Memory Cell
endmodule
