// Logisim project DECODER.circ as structural Verilog: 1 circuit, main circuit main
module main (
  input  EN,
  input  B,
  input  A,
  output Q3,
  output Q2,
  output Q1,
  output Q0
);

  wire not_1_out, not_2_out, not_3_out;

  not not_1 (not_1_out, B);
  not not_2 (not_2_out, EN);
  not not_3 (not_3_out, A);
  and and_1 (Q3, not_2_out, B, A);
  and and_2 (Q2, not_2_out, B, not_3_out);
  and and_3 (Q1, not_2_out, not_1_out, A);
  and and_4 (Q0, not_2_out, not_1_out, not_3_out);
endmodule
