// Logisim project SR_FF.circ as structural Verilog: 1 circuit, main circuit main
module main (
  input  S,
  input  R,
  output Q_BAR,
  output Q
);

  nor nor_1 (Q_BAR, S, Q);
  nor nor_2 (Q, Q_BAR, R);
endmodule
