// Logisim project BusSystem.circ as structural Verilog: 1 circuit, main circuit main
module main (
  input  EN,
  input  [1:0] SEL,
  input  SR0,
  input  P0,
  input  EN0,
  input  R0,
  input  SR1,
  input  P1,
  input  EN1,
  input  R1,
  input  SR2,
  input  P2,
  input  EN2,
  input  R2,
  input  SR3,
  input  P3,
  input  EN3,
  input  R3,
  output D0,
  output D1,
  output D2,
  output D3
);

  wire CLK_out, R0_d0, R0_d1, R0_d2, R0_serial_out, R1_d0, R1_d1, R1_d2, R1_serial_out, R2_d0, R2_d1, R2_d2,
       R2_serial_out, R3_d0, R3_d1, R3_d2, R3_serial_out;

  Clock CLK (.out(CLK_out));
  Multiplexer #(.select(2), .disabled(0)) multiplexer_1 (
    .in0(R0_d0), .in1(R1_d0), .in2(R2_d0), .in3(R3_d0), .out(D0), .sel(SEL), .en(EN));
  SISO_main u_R0 (
    .SERIAL_IN(SR0), .CLK(CLK_out), .PRESET(P0), .EN(EN0), .RESET(R0), .D0(R0_d0), .D1(R0_d1), .D2(R0_d2),
    .SERIAL_OUT(R0_serial_out));
  Multiplexer #(.select(2), .disabled(0)) multiplexer_2 (
    .in0(R0_d1), .in1(R1_d1), .in2(R2_d1), .in3(R3_d1), .out(D1), .sel(SEL), .en(EN));
  SISO_main u_R1 (
    .SERIAL_IN(SR1), .CLK(CLK_out), .PRESET(P1), .EN(EN1), .RESET(R1), .D0(R1_d0), .D1(R1_d1), .D2(R1_d2),
    .SERIAL_OUT(R1_serial_out));
  SISO_main u_R2 (
    .SERIAL_IN(SR2), .CLK(CLK_out), .PRESET(P2), .EN(EN2), .RESET(R2), .D0(R2_d0), .D1(R2_d1), .D2(R2_d2),
    .SERIAL_OUT(R2_serial_out));
  Multiplexer #(.select(2), .disabled(0)) multiplexer_3 (
    .in0(R0_d2), .in1(R1_d2), .in2(R2_d2), .in3(R3_d2), .out(D2), .sel(SEL), .en(EN));
  Multiplexer #(.select(2), .disabled(0)) multiplexer_4 (
    .in0(R0_serial_out), .in1(R1_serial_out), .in2(R2_serial_out), .in3(R3_serial_out), .out(D3), .sel(SEL),
    .en(EN));
  SISO_main u_R3 (
    .SERIAL_IN(SR3), .CLK(CLK_out), .PRESET(P3), .EN(EN3), .RESET(R3), .D0(R3_d0), .D1(R3_d1), .D2(R3_d2),
    .SERIAL_OUT(R3_serial_out));

  // Notes on the sheet:
  //   20162121023
  //   BDA
  //   Prajapati Yash P.
  //   Common Bus System
  //   Batch-23
endmodule
