// Logisim project SISO.circ as structural Verilog: 1 circuit, main circuit main
module main (
  input  SERIAL_IN,
  input  CLK,
  input  PRESET,
  input  EN,
  input  RESET,
  output D0,
  output D1,
  output D2,
  output SERIAL_OUT
);

  wire JK0_qn, JK1_qn, JK2_qn, not_1_out;

  not not_1 (not_1_out, SERIAL_IN);
  J_K_Flip_Flop JK0 (
    .J(SERIAL_IN), .clk(CLK), .K(not_1_out), .Q(D0), .Qn(JK0_qn), .preset(PRESET), .en(EN), .reset(RESET));
  J_K_Flip_Flop JK1 (.J(D0), .clk(CLK), .K(JK0_qn), .Q(D1), .Qn(JK1_qn), .preset(PRESET), .en(EN), .reset(RESET));
  J_K_Flip_Flop JK2 (.J(D1), .clk(CLK), .K(JK1_qn), .Q(D2), .Qn(JK2_qn), .preset(PRESET), .en(EN), .reset(RESET));
  J_K_Flip_Flop JK3 (
    .J(D2), .clk(CLK), .K(JK2_qn), .Q(SERIAL_OUT), .preset(PRESET), .en(EN), .reset(RESET));  // open: Qn

  // Notes on the sheet:
  //   PRAJAPATI YASH P.
  //   20162121023
  //   BDA
  //   SISO
  //   PRAC-8
endmodule
