// Logisim project ALU.circ as structural Verilog: 1 circuit, main circuit main
module main (
  input  A3,
  input  B3,
  input  A2,
  input  B2,
  input  A1,
  input  B1,
  input  A0,
  input  B0,
  input  Cin,
  input  O,
  input  [1:0] PR,
  input  EN,
  output S4,
  output S3,
  output S2,
  output S1,
  output S0
);

  wire and_1_out, and_2_out, and_3_out, and_4_out, main_1_bout, main_1_s, main_2_bout, main_2_s, main_3_bout,
       main_3_s, main_4_bout, main_4_s, multiplexer_1_out, multiplexer_2_out, multiplexer_3_out,
       multiplexer_4_out, multiplexer_5_out, multiplexer_6_out, multiplexer_7_out, multiplexer_8_out,
       not_1_out, not_2_out, not_3_out, not_4_out, not_5_out, not_6_out, not_7_out, not_8_out, not_9_out,
       not_10_out, or_1_out, or_2_out, or_3_out, or_4_out, pull_resistor_1_node, xor_1_out, xor_2_out,
       xor_3_out, xor_4_out;

  Pull_Resistor #(.pull(1)) pull_resistor_1 (.node(pull_resistor_1_node));
  not not_1 (not_1_out, pull_resistor_1_node);
  and and_1 (and_1_out, A3, B3);
  or or_1 (or_1_out, A3, B3);
  xor xor_1 (xor_1_out, A3, B3);
  not not_2 (not_2_out, A3);
  and and_2 (and_2_out, A2, B2);
  or or_2 (or_2_out, A2, B2);
  xor xor_2 (xor_2_out, A2, B2);
  not not_3 (not_3_out, A2);
  and and_3 (and_3_out, A1, B1);
  or or_3 (or_3_out, A1, B1);
  xor xor_3 (xor_3_out, A1, B1);
  not not_4 (not_4_out, A1);
  and and_4 (and_4_out, A0, B0);
  or or_4 (or_4_out, A0, B0);
  xor xor_4 (xor_4_out, A0, B0);
  not not_5 (not_5_out, A0);
  not not_6 (not_6_out, B3);
  not not_7 (not_7_out, B2);
  not not_8 (not_8_out, B1);
  not not_9 (not_9_out, B0);
  Multiplexer #(.select(2), .disabled(0)) multiplexer_1 (
    .in0(B3), .in1(not_6_out), .in2(not_1_out), .in3(pull_resistor_1_node), .out(multiplexer_1_out),
    .sel(PR), .en(not_10_out));
  Multiplexer #(.select(2), .disabled(0)) multiplexer_2 (
    .in0(B2), .in1(not_7_out), .in2(not_1_out), .in3(pull_resistor_1_node), .out(multiplexer_2_out),
    .sel(PR), .en(not_10_out));
  Multiplexer #(.select(2), .disabled(0)) multiplexer_3 (
    .in0(B1), .in1(not_8_out), .in2(not_1_out), .in3(pull_resistor_1_node), .out(multiplexer_3_out),
    .sel(PR), .en(not_10_out));
  Multiplexer #(.select(2), .disabled(0)) multiplexer_4 (
    .in0(B0), .in1(not_9_out), .in2(not_1_out), .in3(pull_resistor_1_node), .out(multiplexer_4_out),
    .sel(PR), .en(not_10_out));
  not not_10 (not_10_out, O);
  Multiplexer #(.select(2)) multiplexer_5 (
    .in0(and_1_out), .in1(or_1_out), .in2(xor_1_out), .in3(not_2_out), .out(multiplexer_5_out), .sel(PR),
    .en(O));
  Multiplexer #(.select(2)) multiplexer_6 (
    .in0(and_2_out), .in1(or_2_out), .in2(xor_2_out), .in3(not_3_out), .out(multiplexer_6_out), .sel(PR),
    .en(O));
  Multiplexer #(.select(2)) multiplexer_7 (
    .in0(and_3_out), .in1(or_3_out), .in2(xor_3_out), .in3(not_4_out), .out(multiplexer_7_out), .sel(PR),
    .en(O));
  Multiplexer #(.select(2)) multiplexer_8 (
    .in0(and_4_out), .in1(or_4_out), .in2(xor_4_out), .in3(not_5_out), .out(multiplexer_8_out), .sel(PR),
    .en(O));
  Full_Adder_main main_1 (.A(A3), .B(multiplexer_1_out), .Cin(main_2_bout), .S(main_1_s), .Bout(main_1_bout));
  Full_Adder_main main_2 (.A(A2), .B(multiplexer_2_out), .Cin(main_3_bout), .S(main_2_s), .Bout(main_2_bout));
  Full_Adder_main main_3 (.A(A1), .B(multiplexer_3_out), .Cin(main_4_bout), .S(main_3_s), .Bout(main_3_bout));
  Full_Adder_main main_4 (.A(A0), .B(multiplexer_4_out), .Cin(Cin), .S(main_4_s), .Bout(main_4_bout));
  Multiplexer multiplexer_9 (.in0(main_1_bout), .in1(1'b0), .out(S4), .sel(O), .en(EN));
  Multiplexer multiplexer_10 (.in0(main_1_s), .in1(multiplexer_5_out), .out(S3), .sel(O), .en(EN));
  Multiplexer multiplexer_11 (.in0(main_2_s), .in1(multiplexer_6_out), .out(S2), .sel(O), .en(EN));
  Multiplexer multiplexer_12 (.in0(main_3_s), .in1(multiplexer_7_out), .out(S1), .sel(O), .en(EN));
  Multiplexer multiplexer_13 (.in0(main_4_s), .in1(multiplexer_8_out), .out(S0), .sel(O), .en(EN));

  // Notes on the sheet:
  //   Prajapati Yash P.
  //   20162121023(BDA)
  //   Practical-9
  //   ALU
endmodule
