// Logisim project HA.circ as structural Verilog: 1 circuit, main circuit main
module main (
  input  A,
  input  B,
  output Carry,
  output SUM
);

  and and_1 (Carry, A, B);
  xor xor_1 (SUM, A, B);

  // Notes on the sheet:
  //   HALF ADDER
  //   20162121023 (BDA)
  //   PRAJAPATI YASH P.
endmodule
