// Logisim project practical_exam.circ as structural Verilog: 1 circuit, main circuit main
module main (
  input  A3,
  input  A2,
  input  A1,
  input  A0,
  input  B3,
  input  B2,
  input  B1,
  input  B0,
  output S7,
  output S6,
  output S5,
  output S4,
  output S3,
  output S2,
  output S1,
  output S0
);

  wire _1_out, _2_out, _3_out, _4_out, _5_out, _6_out, _7_out, _8_out, _9_out, _10_out, _11_out, _12_out,
       _13_out, _14_out, _15_out, main_2_cout, main_2_sum, main_3_cout, main_4_cout, main_4_sum, main_5_cout,
       main_5_sum, main_6_carry, main_7_cout, main_8_carry, main_8_sum, main_9_cout, main_9_sum,
       main_10_carry, main_10_sum, main_11_cout, main_12_carry;

  and _15 (_15_out, B3, A3);
  and _14 (_14_out, B3, A2);
  FA_main main_1 (.A(main_2_cout), .B(_15_out), .Cin(main_3_cout), .SUM(S6), .Cout(S7));
  and _13 (_13_out, B2, A3);
  and _12 (_12_out, B3, A1);
  FA_main main_2 (.A(_13_out), .B(_14_out), .Cin(main_4_cout), .SUM(main_2_sum), .Cout(main_2_cout));
  FA_main main_3 (.A(main_5_cout), .B(main_2_sum), .Cin(main_6_carry), .SUM(S5), .Cout(main_3_cout));
  and _11 (_11_out, B2, A2);
  FA_main main_4 (.A(_10_out), .B(_11_out), .Cin(main_8_carry), .SUM(main_4_sum), .Cout(main_4_cout));
  FA_main main_5 (.A(main_4_sum), .B(_12_out), .Cin(main_9_cout), .SUM(main_5_sum), .Cout(main_5_cout));
  HA_main main_6 (.A(main_7_cout), .B(main_5_sum), .Carry(main_6_carry), .SUM(S4));
  and _9 (_9_out, B3, A0);
  and _10 (_10_out, B1, A3);
  and _8 (_8_out, B2, A1);
  FA_main main_7 (.A(main_9_sum), .B(_9_out), .Cin(main_11_cout), .SUM(S3), .Cout(main_7_cout));
  and _7 (_7_out, B1, A2);
  and _6 (_6_out, B0, A3);
  HA_main main_8 (.A(_6_out), .B(_7_out), .Carry(main_8_carry), .SUM(main_8_sum));
  FA_main main_9 (.A(main_8_sum), .B(_8_out), .Cin(main_10_carry), .SUM(main_9_sum), .Cout(main_9_cout));
  and _4 (_4_out, B1, A1);
  and _5 (_5_out, B2, A0);
  and _3 (_3_out, B0, A2);
  HA_main main_10 (.A(_3_out), .B(_4_out), .Carry(main_10_carry), .SUM(main_10_sum));
  FA_main main_11 (.A(main_10_sum), .B(_5_out), .Cin(main_12_carry), .SUM(S2), .Cout(main_11_cout));
  and _2 (_2_out, B1, A0);
  and _1 (_1_out, B0, A1);
  HA_main main_12 (.A(_1_out), .B(_2_out), .Carry(main_12_carry), .SUM(S1));
  and _0 (S0, B0, A0);

  // Notes on the sheet:
  //   Batch-23
  //   Prajapati Yash P.
  //   20162121023 (BDA)
  //   COMBINATIONAL MULTIPLIER
endmodule
