// Logisim project ADDER.circ as structural Verilog: 1 circuit, main circuit main
module main (
  input  A,
  input  B,
  input  Cin,
  output SUM,
  output Cout
);

  wire and_1_out, and_2_out, xor_1_out;

  xor xor_1 (xor_1_out, A, B);
  xor xor_2 (SUM, xor_1_out, Cin);
  and and_1 (and_1_out, Cin, xor_1_out);
  and and_2 (and_2_out, A, B);
  or or_1 (Cout, and_1_out, and_2_out);

  // Notes on the sheet:
  //   PRAJAPATI YASH P. (BDA)
  //   20162121023
  //   ADDER CIRCUIT
  //   PRACTICAL EXAM
  //   SEM-2
endmodule
